# Fritzing sketch estado-indefinido (saved by Fritzing 0.9.2b)
breadboards: 1

parts:
  Part1 = Arduino Uno (Rev3)
  S3 = Pushbutton [package="[THT]"]

nets:
  N1: Part1.D13/SCK, Part1.5V, S3.Pin_3, S3.Pin_4
  N2: S3.Pin_1, S3.Pin_2
