# Fritzing sketch push-button-protoboard (saved by Fritzing 0.9.3b)
breadboards: 1

parts:
  Componente1 = Arduino Uno (Rev3)
  S1 = Pushbutton [package="[SMD]"]
  R1 = Resistor [tolerance=±5% resistance=15k package=THT]

nets:
  N1: Componente1.D13/SCK, S1.Pin_3, S1.Pin_4, R1.Pin_1
  N2: Componente1.GND, S1.Pin_1, S1.Pin_2
  N3: Componente1.5V, R1.Pin_0

notes:
  Resistor de 10 ohms
